# Fritzing sketch Untitled Sketch (saved by Fritzing 0.9.3b)

parts:
  Part1 = Arduino Uno (Rev3)
  S1 = H-Bridge with L298N
  M1 = DC Motor  # not connected
  M2 = DC Motor
  BAT1 = BC9VPC [package=bc9vpc]
  HC-SR04_Sensor_1 = HC-SR04 Ultrasonic Distance Sensor

nets:
  N1: Part1.D8, S1.IN1
  N2: Part1.D10_PWM/SS, HC-SR04_Sensor_1.ECHO
  N3: Part1.D11_PWM/MOSI, HC-SR04_Sensor_1.TRIG
  N4: Part1.D4, S1.IN4
  N5: Part1.D5_PWM, S1.IN3
  N6: Part1.D6_PWM, S1.IN2
  5V: Part1.5V, HC-SR04_Sensor_1.VCC
  GND: Part1.GND, S1.GND, BAT1.V-, HC-SR04_Sensor_1.GND
  VIN: Part1.VIN, S1.5V
  N7: S1.12V, BAT1.V+
  N8: S1.OUT4-Motor2, M2.pin_1

notes:
  Arduino pins can be connected to your own liking as long as you make sure you the changes are aslo made in the code.
  Both enable pins should be connected to pulse width modulation(pwm) pins.
  to enable you to move the two motors at different speeds for turning
  -motors should be 5v DC

custom parts:
  H-Bridge with L298N: h-bridge

// code stored in the sketch: avoid_obstacle.ino
int trigger_pin = 11;

int echo_pin = 10;



int time;

int distance; 

// Motor A
 
int enA = 9;
int in1 = 8;
int in2 = 7;
 
// Motor B
 
int enB = 3;
int in3 = 4;
int in4 = 5;



void setup ( ) {

        Serial.begin (9600); 

        pinMode (trigger_pin, OUTPUT); 

        pinMode (echo_pin, INPUT);

        pinMode(enA, OUTPUT);
        pinMode(enB, OUTPUT);
        pinMode(in1, OUTPUT);
        pinMode(in2, OUTPUT);
        pinMode(in3, OUTPUT);
        pinMode(in4, OUTPUT);
 




}




void loop ( ) {

    digitalWrite (trigger_pin, HIGH);

    delayMicroseconds (5);

    digitalWrite (trigger_pin, LOW);

    time = pulseIn (echo_pin, HIGH);

    distance = (time * 0.034) / 2;


    analogWrite(enA, 200);
    analogWrite(enB, 200);

              
    digitalWrite(in1, LOW);
    digitalWrite(in2, HIGH);
   
    // Set speed to 200 out of possible range 0~255
   

    // Turn on motor B
   
    digitalWrite(in3, LOW);
    digitalWrite(in4, HIGH);
   
    // Set speed to 200 out of possible range 0~255
   
    

   
 

    

  if (distance <= 20)     

        {



  digitalWrite(in1, HIGH);
  digitalWrite(in2, LOW);  
  digitalWrite(in3, HIGH);
  digitalWrite(in4, LOW);

  analogWrite(enA, 0);      // reverse for u turn
  analogWrite(enB, 100);

  delay(1000);

  digitalWrite(in1, LOW); // forward again
  digitalWrite(in2, HIGH);  
  digitalWrite(in3, LOW);
  digitalWrite(in4, HIGH);

  analogWrite(enA, 200);   // both motors same speed
  analogWrite(enB, 200);

       
        }

  else {               //else keep moving forward
    


    digitalWrite(in1, LOW);
    digitalWrite(in2, HIGH);  
    digitalWrite(in3, LOW);
    digitalWrite(in4, HIGH);


  } 

  }
