# Fritzing sketch led_traffic (saved by Fritzing 0.9.3b)
breadboards: 1

parts:
  Part1 = Arduino Uno (Rev3) - ICSP
  LED3 = LED - 5mm [color="Green (565nm)" package="5 mm [THT]"]
  LED4 = LED - 5mm [color="Red (633nm)" package="5 mm [THT]"]
  LED2 = smd LED [color="Orange (605nm)" package="1206 [SMD]"]

nets:
  N1: Part1.ICSP_MOSI, Part1.D11_PWM/MOSI, LED4.anode
  N2: Part1.D12/MISO, LED2.anode
  N3: Part1.D13/SCK, LED3.anode
  N4: Part1.GND, LED3.cathode, LED4.cathode, LED2.cathode

notes:
  1. Ground the negative pins of the led
  2. connect the positive pins to digital pins 13, 12 , 11
  3.you can connect the green , orange, red LED's
  We will connect the arduino and use python package pyfirmata and pyserial to communicate with the arduino

// code stored in the sketch: led_traffic.ino
try:
    from pyfirmata import Arduino , util
except:
    import pip
    pip.main(['install','pyfirmata'])   # install pyfirmata # do not worry about this it is just how we do this in linux



import time                # module to tell clock time

redled_pin1 = 11           #we connect to the pins for communication between arduino and computer
orangeled_pin2 = 12
blueled_pin3 = 13          # pin on the Arduino to be used
port = '/dev/ttyACM0'  # com port for Arduino  
board = Arduino(port)  # creates Arduino board object variable


board.digital[pin1].write(1)   # writes high voltage value to pin, LED_red on
time.sleep(1)                  # sleeps for 1 second
board.digital[pin].write(0)    # turn off led_red

board.digital[pin2].write(1)   # writes high voltage value to pin, LED_orange on
time.sleep(1)                  # sleeps for 1 second
board.digital[pin2].write(0)		# turn off led_orange

board.digital[pin3].write(1)   # writes high voltage value to pin, LED_green on
time.sleep(1)                  # sleeps for 1 second
board.digital[pin3].write(0)   # turn off led_red
